# Fritzing sketch POC lumiere (saved by Fritzing 0.9.3b)
circuit board: 8.46667cm x 5.64444cm
breadboards: 1

parts:
  Composant1 = Arduino Uno (Rev3)
  R1 = Resistor [tolerance=±5% resistance=10k package=THT]
  R2 = Photocell (LDR) [package=THT]

nets:
  N1: Composant1.A0, R1.Pin_1, R2.pin_0
  N2: Composant1.GND, R1.Pin_0
  N3: Composant1.5V, R2.pin_1

// code stored in the sketch: POC lumiere.ino
// Pour enlever le mode debug, commenter la ligne suivante
#define DebugMode 1

const int sensorPin = 0;                  //pin entrée analogique de la resistance photosensible

const int lightPackageOpened = 200;       //seuil au dessus du quel le paquet est considéré comme ouvert. A changer selon le paquet
const int noLight = 200, lowLight = 500;  //constante de description des seuil de luminosité

int lightLevel;                           //niveau de la lumiere mesurer (val entre 0 et 1023)
bool packageOpened;                       //variable désignant l'état de paquet (ouvert/fermé)
String lightState;                        //variable de description de la luminosité


void setup()
{
    Serial.begin(9600);
}


void loop()
{
    // Méthodes permetant de récuperer les différentes valeurs de la luminosité.
    // Doivent être utilisées dans cet ordre.
    /////////////////////////////////////////////////////////////////////////////
    getLightLevel();
    getLightDescription();
    getPackageOpened();
    /////////////////////////////////////////////////////////////////////////////

    #ifdef DebugMode
      Serial.print("Light level : ");
      Serial.println(lightLevel);
      Serial.print("Light state : ");
      Serial.println(lightState);
      Serial.print("Package opened ? : ");
      Serial.println(packageOpened);
      delay (1000);
    #endif
}


// Permet de renseigner la valeur brute de la lumière dans la variable lightLevel
void getLightLevel()
{ 
    lightLevel = analogRead(sensorPin);
}

// Permet de renseigner la valeur texte de l'état de la lumière dans la valeur lightState
void getLightDescription()
{
    // Si la valeur de la lumière est inférieure au seuil noLight
    if (lightLevel <= noLight)
    {
        lightState = "Gloomy";
    }
    // Si la valeur de la lumière est inférieure au seuil lowLight mais supérieure au seuil noLight
    else if (lightLevel <= lowLight and lightLevel > noLight)
    {
        lightState = "Low light";
    }
    // Si la valeur de la lumière est supérieure au seuil lowLight
    else 
    {
        lightState = "High light";
    }
}

// Permet de renseigner le bool définisant si le paquet est ouvert
void getPackageOpened()
{
    if (lightLevel > lightPackageOpened)
    {
        packageOpened = true;
    }
    else 
    {
        packageOpened = false;
    }
}
