# Fritzing sketch resetBtn (saved by Fritzing 0.9.3b)
breadboards: 1

parts:
  Composant1 = Arduino Uno (Rev3)
  S1 = Pushbutton [package="[THT]"]
  R1 = Resistor [tolerance=±5% resistance=10k package=THT]

nets:
  N1: Composant1.D3_PWM, Composant1.5V, S1.Pin_1, S1.Pin_2
  N2: Composant1.GND, R1.Pin_0
  N3: S1.Pin_3, S1.Pin_4, R1.Pin_1
